// Logisim project alu.circ as structural Verilog: 1 circuit, main circuit alu
module alu (
  input  [31:0] A,
  input  [31:0] B,
  input  [3:0] ALUSel,
  output [31:0] Result
);

  wire adder_1_cout, adder_4_cout, comparator_1_lt, xor_2_out;
  wire [4:0] bit_extender_1_out, bit_extender_2_out, bit_extender_3_out;
  wire [31:0] add0, adder_2_out, adder_3_out, adder_4_out, adder_5_out, and1, bit_extender_5_out, divu8,
       mul10, mulh14, mulhu11, multiplexer_1_out, multiplexer_2_out, multiplier_2_cout, multiplier_2_out,
       not_1_out, not_2_out, not_3_out, not_4_out, or2, remu9, sll6, slt7, sra5, srl4, sub12, xor3;

  Adder #(.width(32)) adder_1 (.a(A), .b(B), .out(add0), .cout(adder_1_cout));  // open: cin
  assign and1 = A & B;  // AND_Gate and_1, 32 bits wide
  assign or2 = A | B;  // OR_Gate or_1, 32 bits wide
  assign xor3 = A ^ B;  // XOR_Gate xor_1, 32 bits wide
  Shifter #(.width(32), .shift("lr")) shifter_1 (.in(A), .\dist (bit_extender_1_out), .out(srl4));
  Bit_Extender #(.in_width(32), .out_width(5)) bit_extender_1 (.in(B), .out(bit_extender_1_out));
  assign not_1_out = ~A;  // NOT_Gate not_1, 32 bits wide
  assign not_2_out = ~B;  // NOT_Gate not_2, 32 bits wide
  Bit_Extender #(.in_width(32), .out_width(5)) bit_extender_2 (.in(B), .out(bit_extender_2_out));
  Bit_Extender #(.in_width(32), .out_width(5)) bit_extender_3 (.in(B), .out(bit_extender_3_out));
  Multiplexer #(.width(32), .enable("false")) multiplexer_1 (
    .in0(A), .in1(adder_2_out), .out(multiplexer_1_out), .sel(A[31]));
  Adder #(.width(32)) adder_2 (.a(not_1_out), .b(32'h1), .out(adder_2_out));  // open: cin, cout
  Multiplexer #(.width(32), .enable("false")) multiplexer_2 (
    .in0(B), .in1(adder_3_out), .out(multiplexer_2_out), .sel(B[31]));
  Adder #(.width(32)) adder_3 (.a(not_2_out), .b(32'h1), .out(adder_3_out));  // open: cin, cout
  Shifter #(.width(32), .shift("ar")) shifter_2 (.in(A), .\dist (bit_extender_2_out), .out(sra5));
  Shifter #(.width(32)) shifter_3 (.in(A), .\dist (bit_extender_3_out), .out(sll6));
  assign slt7 = {{31{1'b0}}, comparator_1_lt};  // Bit_Extender bit_extender_4
  Comparator #(.width(32)) comparator_1 (.a(A), .b(B), .lt(comparator_1_lt));  // open: gt, eq
  Divider #(.width(32)) divider_1 (.a(A), .b(B), .out(divu8), .rem(remu9));  // open: upper
  Multiplier #(.width(32)) multiplier_1 (.a(A), .b(B), .out(mul10), .cout(mulhu11));  // open: cin
  Multiplier #(.width(32)) multiplier_2 (
    .a(multiplexer_1_out), .b(multiplexer_2_out), .out(multiplier_2_out), .cout(multiplier_2_cout));  // open: cin
  assign not_3_out = ~multiplier_2_out;  // NOT_Gate not_3, 32 bits wide
  assign bit_extender_5_out = {{31{1'b0}}, adder_4_cout};  // Bit_Extender bit_extender_5
  assign not_4_out = ~multiplier_2_cout;  // NOT_Gate not_4, 32 bits wide
  Multiplexer #(.width(32), .enable("false")) multiplexer_3 (
    .in0(multiplier_2_cout), .in1(adder_5_out), .out(mulh14), .sel(xor_2_out));
  xor xor_2 (xor_2_out, B[31], A[31]);
  Adder #(.width(32)) adder_4 (.a(32'h1), .b(not_3_out), .out(adder_4_out), .cout(adder_4_cout));  // open: cin
  Adder #(.width(32)) adder_5 (.a(bit_extender_5_out), .b(not_4_out), .out(adder_5_out));  // open: cin, cout
  Subtractor #(.width(32)) subtractor_1 (.a(A), .b(B), .out(sub12));  // open: bin, bout
  Multiplexer #(.select(4), .width(32), .enable("false")) multiplexer_4 (
    .in0(add0), .in1(and1), .in2(or2), .in3(xor3), .in4(srl4), .in5(sra5), .in6(sll6), .in7(slt7),
    .in8(divu8), .in9(remu9), .in10(mul10), .in11(mulhu11), .in12(sub12), .in13(B), .in14(mulh14),
    .out(Result), .sel(ALUSel));  // open: in15

  // Other names for the same wires on the sheet: bsel13[31:0] = B

  // Notes on the sheet:
  //   INPUTS to your circuit
  //   DON'T CHANGE THE LOCATIONS OF THE INPUTS AND OUTPUTS!
  //   OUTPUT from your circuit
endmodule
