// Logisim project control_logic.circ as structural Verilog: 1 circuit, main circuit control_logic
module control_logic (
  input  [31:0] inst,
  input  BrEq,
  input  BrLt,
  output PCSel,
  output RegWEn,
  output [2:0] ImmSel,
  output BrUn,
  output ASel,
  output BSel,
  output [3:0] ALUSel,
  output MemRW,
  output [1:0] WBSel
);

  wire and_7_out, and_8_out, and_9_out, and_10_out, and_11_out, and_12_out, ArithType, AUIPC_U_type,
       beq_type, bge_type, bgeu_type, blt_type, bltu_type, bne_type, BranchJump, BrGe, comparator_1_eq,
       comparator_2_eq, comparator_3_eq, comparator_4_eq, comparator_5_eq, comparator_6_eq, JAL_UJ_type,
       JALR_I_type, JumpType, Load_I_type, LUI_U_type, nor_1_out, Norm_I_type, not_1_out, or_8_out, R_type,
       SB_type;
  wire [1:0] multiplexer_2_out, multiplexer_4_out, multiplexer_6_out, multiplexer_7_out, multiplexer_8_out,
       multiplexer_12_out, multiplexer_15_out, multiplexer_17_out, multiplexer_20_out, subOP;
  wire [3:0] adder_1_out, ALU0, ALU1, ALU2, ALU3, ALU4, ALU5, ALU6, ALU7, bit_extender_2_out,
       multiplexer_18_out, multiplexer_19_out;
  wire [6:0] opcode;

  Bit_Extender #(.in_width(32), .out_width(7)) bit_extender_1 (.in(inst), .out(opcode));
  Multiplexer #(.select(2), .width(4), .enable("false")) multiplexer_1 (
    .in0(4'b0000), .in1(4'b1010), .in2(4'b1100), .out(ALU0), .sel(multiplexer_2_out));  // open: in3
  Multiplexer #(.width(2), .enable("false")) multiplexer_2 (
    .in0(2'b00), .in1(subOP), .out(multiplexer_2_out), .sel(R_type));
  Multiplexer #(.select(2), .width(4), .enable("false")) multiplexer_3 (
    .in0(4'b0110), .in1(4'b1110), .out(ALU1), .sel(multiplexer_4_out));  // open: in2, in3
  Multiplexer #(.width(2), .enable("false")) multiplexer_4 (
    .in0(2'b00), .in1(subOP), .out(multiplexer_4_out), .sel(ArithType));
  Multiplexer #(.select(2), .width(4), .enable("false")) multiplexer_5 (
    .in0(4'b0111), .out(ALU2), .sel(multiplexer_6_out));  // open: in1, in2, in3
  Multiplexer #(.width(2), .enable("false")) multiplexer_6 (
    .in0(2'b00), .in1(subOP), .out(multiplexer_6_out), .sel(R_type));
  Comparator #(.width(3), .mode("unsigned")) comparator_1 (
    .a(inst[14:12]), .b(3'b000), .eq(comparator_1_eq));  // open: gt, lt
  Comparator #(.width(3), .mode("unsigned")) comparator_2 (
    .a(inst[14:12]), .b(3'b001), .eq(comparator_2_eq));  // open: gt, lt
  Comparator #(.width(3), .mode("unsigned")) comparator_3 (
    .a(inst[14:12]), .b(3'b100), .eq(comparator_3_eq));  // open: gt, lt
  Comparator #(.width(3), .mode("unsigned")) comparator_4 (
    .a(inst[14:12]), .b(3'b101), .eq(comparator_4_eq));  // open: gt, lt
  Comparator #(.width(3), .mode("unsigned")) comparator_5 (
    .a(inst[14:12]), .b(3'b110), .eq(comparator_5_eq));  // open: gt, lt
  Comparator #(.width(3), .mode("unsigned")) comparator_6 (
    .a(inst[14:12]), .b(3'b111), .eq(comparator_6_eq));  // open: gt, lt
  and and_1 (beq_type, SB_type, comparator_1_eq);
  and and_2 (bne_type, SB_type, comparator_2_eq);
  and and_3 (blt_type, SB_type, comparator_3_eq);
  and and_4 (bge_type, SB_type, comparator_4_eq);
  and and_5 (bltu_type, SB_type, comparator_5_eq);
  and and_6 (bgeu_type, SB_type, comparator_6_eq);
  Comparator #(.width(7), .mode("unsigned")) comparator_7 (.a(opcode), .b(7'b0110011), .eq(R_type));  // open: gt, lt
  Comparator #(.width(7), .mode("unsigned")) comparator_8 (
    .a(opcode), .b(7'b0000011), .eq(Load_I_type));  // open: gt, lt
  Comparator #(.width(7), .mode("unsigned")) comparator_9 (
    .a(opcode), .b(7'b0010011), .eq(Norm_I_type));  // open: gt, lt
  Comparator #(.width(7), .mode("unsigned")) comparator_10 (.a(opcode), .b(7'b0100011), .eq(MemRW));  // open: gt, lt
  Comparator #(.width(7), .mode("unsigned")) comparator_11 (.a(opcode), .b(7'b1100011), .eq(SB_type));  // open: gt, lt
  Comparator #(.width(7), .mode("unsigned")) comparator_12 (
    .a(opcode), .b(7'b0010111), .eq(AUIPC_U_type));  // open: gt, lt
  Comparator #(.width(7), .mode("unsigned")) comparator_13 (
    .a(opcode), .b(7'b0110111), .eq(LUI_U_type));  // open: gt, lt
  Comparator #(.width(7), .mode("unsigned")) comparator_14 (
    .a(opcode), .b(7'b1101111), .eq(JAL_UJ_type));  // open: gt, lt
  Comparator #(.width(7), .mode("unsigned")) comparator_15 (
    .a(opcode), .b(7'b1100111), .eq(JALR_I_type));  // open: gt, lt
  Multiplexer #(.width(2), .enable("false")) multiplexer_7 (
    .in0(2'b01), .in1(subOP), .out(multiplexer_7_out), .sel(R_type));
  Multiplexer #(.width(2), .enable("false")) multiplexer_8 (
    .in0(2'b00), .in1(subOP), .out(multiplexer_8_out), .sel(R_type));
  Multiplexer #(.select(2), .width(4), .enable("false")) multiplexer_9 (
    .in1(4'b1011), .out(ALU3), .sel(multiplexer_7_out));  // open: in0, in2, in3
  Multiplexer #(.select(2), .width(4), .enable("false")) multiplexer_10 (
    .in0(4'b0011), .out(ALU4), .sel(multiplexer_8_out));  // open: in1, in2, in3
  Multiplexer #(.select(2), .width(4), .enable("false")) multiplexer_11 (
    .in0(4'b0100), .in1(4'b1000), .in2(4'b0101), .out(ALU5), .sel(multiplexer_12_out));  // open: in3
  Multiplexer #(.width(2), .enable("false")) multiplexer_12 (
    .in0(2'b00), .in1(subOP), .out(multiplexer_12_out), .sel(ArithType));
  or or_1 (BrUn, bltu_type, bgeu_type);
  nor nor_1 (nor_1_out, BrEq, BrLt);
  Multiplexer #(.select(5), .width(3), .enable("false")) multiplexer_13 (
    .in0(3'b001), .in4(3'b001), .in5(3'b100), .in8(3'b010), .in12(3'b000), .in13(3'b100), .in24(3'b011),
    .in25(3'b001), .in27(3'b101), .out(ImmSel), .sel(opcode[6:2]));  // open: in1, in2, in3, in6, in7, in9, in10, in11, in14, in15, in16, in17, in18, in19, in20, in21, in22, in23, in26, in28, in29, in30, in31
  Multiplexer #(.select(2), .width(4), .enable("false")) multiplexer_14 (
    .in0(4'b0010), .out(ALU6), .sel(multiplexer_15_out));  // open: in1, in2, in3
  Multiplexer #(.width(2), .enable("false")) multiplexer_15 (
    .in0(2'b00), .in1(subOP), .out(multiplexer_15_out), .sel(R_type));
  Multiplexer #(.select(2), .width(4), .enable("false")) multiplexer_16 (
    .in0(4'b0001), .in1(4'b1001), .out(ALU7), .sel(multiplexer_17_out));  // open: in2, in3
  Multiplexer #(.width(2), .enable("false")) multiplexer_17 (
    .in0(2'b00), .in1(subOP), .out(multiplexer_17_out), .sel(R_type));
  or or_2 (BrGe, nor_1_out, BrEq);
  or or_3 (ArithType, Norm_I_type, R_type);
  and and_7 (and_7_out, beq_type, BrEq);
  and and_8 (and_8_out, bne_type, not_1_out);
  not not_1 (not_1_out, BrEq);
  and and_9 (and_9_out, blt_type, BrLt);
  and and_10 (and_10_out, bge_type, BrGe);
  and and_11 (and_11_out, bltu_type, BrLt);
  and and_12 (and_12_out, bgeu_type, BrGe);
  or or_4 (JumpType, JAL_UJ_type, JALR_I_type);
  or or_5 (ASel, SB_type, AUIPC_U_type, JAL_UJ_type);
  Multiplexer #(.select(3), .width(4), .enable("false")) multiplexer_18 (
    .in0(ALU0), .in1(ALU1), .in2(ALU2), .in3(ALU3), .in4(ALU4), .in5(ALU5), .in6(ALU6), .in7(ALU7),
    .out(multiplexer_18_out), .sel(inst[14:12]));
  or or_6 (BranchJump, and_7_out, and_8_out, and_9_out, and_10_out, and_11_out, and_12_out);
  Multiplexer #(.width(4), .enable("false")) multiplexer_19 (
    .in0(4'b0000), .in1(4'b1101), .out(multiplexer_19_out), .sel(LUI_U_type));
  Multiplexer #(.width(2), .enable("false")) multiplexer_20 (
    .in0(2'b00), .in1(2'b10), .out(multiplexer_20_out), .sel(JumpType));
  Multiplexer #(.width(4), .enable("false")) multiplexer_21 (
    .in0(multiplexer_19_out), .in1(multiplexer_18_out), .out(ALUSel), .sel(ArithType));
  Adder #(.width(4)) adder_1 (.a(inst[28:25]), .b(bit_extender_2_out), .out(adder_1_out));  // open: cin, cout
  assign bit_extender_2_out = {{1{1'b0}}, inst[31:29]};  // Bit_Extender bit_extender_2
  or or_7 (PCSel, BranchJump, JumpType);
  not not_2 (BSel, R_type);
  Multiplexer #(.width(2), .enable("false")) multiplexer_22 (
    .in0(2'b01), .in1(multiplexer_20_out), .out(WBSel), .sel(or_8_out));
  or or_8 (or_8_out, JumpType, Load_I_type);
  Bit_Extender #(.in_width(4), .out_width(2), .\type ("zero")) bit_extender_3 (.in(adder_1_out), .out(subOP));
  or or_9 (RegWEn, ArithType, Load_I_type, AUIPC_U_type, LUI_U_type, JumpType);

  // Other names for the same wires on the sheet: func3[2:0] = inst[14:12]; func7[6:0] = inst[31:25]; S_type = MemRW

  // Notes on the sheet:
  //   0x0
  //   0x1
  //   0x2
  //   OPCODE
  //   INPUTS to your circuit
  //   0x3
  //   0x4
  //   0x5
  //   x
  //   x
  //   0x6
  //   0x7
  //   DON'T CHANGE THE LOCATIONS OF THE INPUTS AND OUTPUTS!
  //   OUTPUT from your circuit
  //   x
  //   x
  //   x
  //   x
  //   x
  //   x
endmodule
