// Logisim project cpu.circ as structural Verilog: 1 circuit, main circuit main
module main (
  input  [31:0] INSTRUCTION,
  input  CLOCK,
  output [31:0] PROGRAM_COUNTER,
  output [31:0] ra,
  output [31:0] sp,
  output [31:0] t0,
  output [31:0] t1,
  output [31:0] t2,
  output [31:0] s0,
  output [31:0] s1,
  output [31:0] a0
);

  wire branch_comp_1_breq, branch_comp_1_brlt, comparator_3_lt, comparator_4_eq, control_logic_1_asel,
       control_logic_1_brun, control_logic_1_bsel, control_logic_1_memrw, control_logic_1_regwen, DMEM_p4,
       load_instruction, not_1_out, PCchange, save_instruction, swlt_address, swlt_check;
  wire [1:0] control_logic_1_wbsel, loadAlign, multiplexer_3_out, multiplexer_4_out;
  wire [2:0] control_logic_1_immsel, func3_piped;
  wire [3:0] control_logic_1_alusel;
  wire [6:0] func7_piped, opcode_piped;
  wire [7:0] multiplexer_9_out;
  wire [15:0] multiplexer_5_out;
  wire [24:0] INSTRUCTION_piped;
  wire [31:0] adder_1_out, adder_2_out, ALUoutput, DMEM_p6, Immediate, multiplexer_1_out, multiplexer_2_out,
       multiplexer_7_out, multiplexer_8_out, multiplexer_10_out, PROGRAM_COUNTER_piped, rs1, rs2, WBoutput,
       WBoutputByte, WBoutputHalfWord, WBoutputProcessed;

  control_logic control_logic_1 (
    .BSel(control_logic_1_bsel), .BrUn(control_logic_1_brun), .RegWEn(control_logic_1_regwen),
    .ImmSel(control_logic_1_immsel), .ASel(control_logic_1_asel), .PCSel(PCchange),
    .BrLt(branch_comp_1_brlt), .BrEq(branch_comp_1_breq),
    .inst({func7_piped, INSTRUCTION_piped[24:15], func3_piped, INSTRUCTION_piped[11:0]}),
    .ALUSel(control_logic_1_alusel), .MemRW(control_logic_1_memrw), .WBSel(control_logic_1_wbsel));
  Adder #(.width(32)) adder_1 (.a(PROGRAM_COUNTER), .b(32'h4), .out(adder_1_out));  // open: cin, cout
  Multiplexer #(.width(32), .enable("false")) multiplexer_1 (
    .in0(adder_1_out), .in1(ALUoutput), .out(multiplexer_1_out), .sel(PCchange));
  Register #(.width(32)) PC (.D(multiplexer_1_out), .clk(CLOCK), .Q(PROGRAM_COUNTER));  // open: en, clr
  imm_gen imm_gen_1 (
    .ImmSel(control_logic_1_immsel), .imm(Immediate),
    .inst({func7_piped, INSTRUCTION_piped[24:15], func3_piped, INSTRUCTION_piped[11:0]}));
  Bit_Extender #(.in_width(32), .out_width(7)) bit_extender_1 (
    .in({func7_piped, INSTRUCTION_piped[24:15], func3_piped, INSTRUCTION_piped[11:0]}), .out(opcode_piped));
  Comparator #(.width(7)) comparator_1 (.a(opcode_piped), .b(7'b0000011), .eq(load_instruction));  // open: gt, lt
  Comparator #(.width(7)) comparator_2 (.a(opcode_piped), .b(7'b0100011), .eq(save_instruction));  // open: gt, lt
  branch_comp branch_comp_1 (
    .BrEq(branch_comp_1_breq), .BrUn(control_logic_1_brun), .rs1(rs1), .BrLt(branch_comp_1_brlt), .rs2(rs2));
  Register #(.width(32)) register_1 (
    .D(multiplexer_2_out), .clk(CLOCK),
    .Q({func7_piped, INSTRUCTION_piped[24:15], func3_piped, INSTRUCTION_piped[11:0]}));  // open: en, clr
  Multiplexer #(.width(32), .enable("false")) multiplexer_2 (
    .in0(INSTRUCTION), .in1(32'h13), .out(multiplexer_2_out), .sel(PCchange));
  Bit_Extender #(.in_width(32), .out_width(2)) bit_extender_2 (.in(Immediate), .out(loadAlign));
  Multiplexer #(.select(2), .width(2), .enable("false")) multiplexer_3 (
    .in0(2'b10), .in1(2'b01), .in2(2'b00), .out(multiplexer_3_out), .sel(func3_piped[1:0]));  // open: in3
  Multiplexer #(.width(2), .enable("false")) multiplexer_4 (
    .in0(2'b00), .in1(multiplexer_3_out), .out(multiplexer_4_out), .sel(load_instruction));
  Multiplexer #(.select(2), .width(16), .enable("false")) multiplexer_5 (
    .in0(WBoutput[15:0]), .in2(WBoutput[31:16]), .out(multiplexer_5_out), .sel(loadAlign));  // open: in1, in3
  Multiplexer #(.select(2), .width(32), .enable("false")) multiplexer_6 (
    .in0(WBoutput), .in1(WBoutputHalfWord), .in2(WBoutputByte), .out(WBoutputProcessed),
    .sel(multiplexer_4_out));  // open: in3
  assign WBoutputHalfWord = {{16{multiplexer_5_out[15]}}, multiplexer_5_out};  // Bit_Extender bit_extender_3
  regfile_main RegFile (
    .rs2(INSTRUCTION_piped[24:20]), .rd(INSTRUCTION_piped[11:7]), .Read_Data_1(rs1), .Read_Data_2(rs2),
    .ra(ra), .sp(sp), .t0(t0), .t1(t1), .t2(t2), .s0(s0), .s1(s1), .a0(a0), .rs1(INSTRUCTION_piped[19:15]),
    .Write_Data(WBoutputProcessed), .RegWEn(control_logic_1_regwen), .clk(CLOCK));
  Multiplexer #(.width(32), .enable("false")) multiplexer_7 (
    .in0(rs2), .in1(Immediate), .out(multiplexer_7_out), .sel(control_logic_1_bsel));
  Multiplexer #(.width(32), .enable("false")) multiplexer_8 (
    .in0(rs1), .in1(PROGRAM_COUNTER_piped), .out(multiplexer_8_out), .sel(control_logic_1_asel));
  Multiplexer #(.select(2), .width(8), .enable("false")) multiplexer_9 (
    .in0(WBoutput[7:0]), .in1(WBoutput[15:8]), .in2(WBoutput[23:16]), .in3(WBoutput[31:24]),
    .out(multiplexer_9_out), .sel(loadAlign));
  alu Arithmetic_Logic_Unit (
    .Result(ALUoutput), .ALUSel(control_logic_1_alusel), .A(multiplexer_8_out), .B(multiplexer_7_out));
  Register #(.width(32)) register_2 (.D(PROGRAM_COUNTER), .clk(CLOCK), .Q(PROGRAM_COUNTER_piped));  // open: en, clr
  not not_1 (not_1_out, comparator_3_lt);
  Comparator #(.width(32)) comparator_3 (.a(rs2), .b(Immediate), .lt(comparator_3_lt));  // open: gt, eq
  Comparator #(.width(3)) comparator_4 (.a(func3_piped), .b(3'b111), .eq(comparator_4_eq));  // open: gt, lt
  assign WBoutputByte = {{24{multiplexer_9_out[7]}}, multiplexer_9_out};  // Bit_Extender bit_extender_4
  and and_1 (swlt_check, save_instruction, not_1_out, comparator_4_eq);
  and and_2 (swlt_address, comparator_3_lt, comparator_4_eq, save_instruction);
  Multiplexer #(.width(32), .enable("false")) multiplexer_10 (
    .in0(ALUoutput), .in1(rs1), .out(multiplexer_10_out), .sel(swlt_address));
  // mem_main DMEM: pin names not known; wires that end beside it: multiplexer_10_out, rs2, CLOCK, DMEM_p4, DMEM_p4, DMEM_p6
  Multiplexer #(.enable("false")) multiplexer_11 (
    .in0(control_logic_1_memrw), .in1(1'b0), .out(DMEM_p4), .sel(swlt_check));
  Adder #(.width(32)) adder_2 (.a(PROGRAM_COUNTER_piped), .b(32'h4), .out(adder_2_out));  // open: cin, cout
  Multiplexer #(.select(2), .width(32), .enable("false")) multiplexer_12 (
    .in0(DMEM_p6), .in1(ALUoutput), .in2(adder_2_out), .out(WBoutput), .sel(control_logic_1_wbsel));  // open: in3

  // Other names for the same wires on the sheet: clk = CLOCK;
  //   INSTRUCTION_piped (some bits) = {func7_piped, func3_piped}

  // Notes on the sheet:
  //   OPCODE
  //   Output
  //   IMEM (do **NOT** move this)
  //   Inputs
  //   It is OK to move the PC, RegFile, ALU, MEM, Branch Comp, Imm Gen, and Control Logic to wherever is most convenient for you when constructing your CPU, and to delete this text
  //   Inputs/Outputs for testing. Do **NOT** move these.
endmodule
