// Logisim project imm_gen.circ as structural Verilog: 1 circuit, main circuit imm_gen
module imm_gen (
  input  [31:0] inst,
  input  [2:0] ImmSel,
  output [31:0] imm
);

  wire [31:0] bit_extender_1_out, bit_extender_2_out, bit_extender_3_out, bit_extender_4_out,
       bit_extender_5_out, shifter_1_out, shifter_2_out, shifter_3_out;

  assign bit_extender_1_out = {{20{inst[31]}}, inst[31:20]};  // Bit_Extender bit_extender_1
  assign bit_extender_2_out = {{20{inst[31]}}, {inst[31:25], inst[11:7]}};  // Bit_Extender bit_extender_2
  assign bit_extender_3_out = {{20{inst[31]}}, {inst[31], inst[7], inst[30:25], inst[11:8]}};  // Bit_Extender bit_extender_3
  Shifter #(.width(32)) shifter_1 (.in(bit_extender_3_out), .\dist (5'b00001), .out(shifter_1_out));
  Shifter #(.width(32)) shifter_2 (.in(bit_extender_4_out), .\dist (5'b01100), .out(shifter_2_out));
  assign bit_extender_4_out = {{12{inst[31]}}, inst[31:12]};  // Bit_Extender bit_extender_4
  Shifter #(.width(32)) shifter_3 (.in(bit_extender_5_out), .\dist (5'b00001), .out(shifter_3_out));
  assign bit_extender_5_out = {{12{inst[31]}}, {inst[31], inst[19:12], inst[20], inst[30:21]}};  // Bit_Extender bit_extender_5
  Multiplexer #(.select(3), .width(32), .enable("false")) multiplexer_1 (
    .in1(bit_extender_1_out), .in2(bit_extender_2_out), .in3(shifter_1_out), .in4(shifter_2_out),
    .in5(shifter_3_out), .out(imm), .sel(ImmSel));  // open: in0, in6, in7

  // Notes on the sheet:
  //   INPUTS to your circuit
  //   R = 000
  //   I = 001
  //   S = 010
  //   SB = 011
  //   U = 100
  //   UJ = 101
  //   I format
  //   S format
  //   SB format
  //   U format
  //   UJ format
  //   DON'T CHANGE THE LOCATIONS OF THE INPUTS AND OUTPUTS!
  //   OUTPUT from your circuit
endmodule
